// Logisim project main.circ as structural Verilog
module main (
);

  wire a_key, cell_drawer_1_explose, cell_drawer_1_selected, cell_drawer_2_explose, cell_drawer_2_selected,
       cell_drawer_3_explose, cell_drawer_3_selected, cell_drawer_4_explose, cell_drawer_4_selected,
       cell_drawer_5_explose, cell_drawer_5_selected, cell_drawer_6_explose, cell_drawer_6_selected,
       cell_drawer_7_explose, cell_drawer_7_selected, cell_drawer_8_explose, cell_drawer_8_selected,
       cell_drawer_9_selected, cell_drawer_10_selected, cell_drawer_11_selected, cell_drawer_12_selected,
       cell_drawer_13_selected, cell_drawer_14_selected, cell_drawer_15_selected, cell_drawer_16_selected,
       cell_drawer_17_selected, cell_drawer_18_selected, cell_drawer_19_selected, cell_drawer_20_selected,
       cell_drawer_21_selected, cell_drawer_22_selected, cell_drawer_23_selected, cell_drawer_24_selected,
       cell_drawer_25_selected, cell_drawer_26_selected, cell_drawer_27_selected, cell_drawer_28_selected,
       cell_drawer_29_selected, cell_drawer_30_selected, cell_drawer_31_selected, cell_drawer_32_selected,
       cell_drawer_33_selected, cell_drawer_34_selected, cell_drawer_35_selected, cell_drawer_36_selected,
       cell_drawer_37_selected, cell_drawer_38_selected, cell_drawer_39_selected, cell_drawer_40_selected,
       cell_drawer_41_selected, cell_drawer_42_selected, cell_drawer_43_selected, cell_drawer_44_selected,
       cell_drawer_45_selected, cell_drawer_46_selected, cell_drawer_47_selected, cell_drawer_48_selected,
       cell_drawer_49_selected, cell_drawer_50_selected, cell_drawer_51_selected, cell_drawer_52_selected,
       cell_drawer_53_selected, cell_drawer_54_selected, cell_drawer_55_selected, cell_drawer_56_selected,
       cell_drawer_57_selected, cell_drawer_58_selected, cell_drawer_59_selected, cell_drawer_60_selected,
       cell_drawer_61_selected, cell_drawer_62_selected, cell_drawer_63_selected, cell_drawer_64_selected,
       d_key, flag_key, open_key, r_key, s_key, w_key;
  wire [3:0] cell_drawer_1_img, cell_drawer_2_img, cell_drawer_3_img, cell_drawer_4_img, cell_drawer_5_img,
       cell_drawer_6_img, cell_drawer_7_img, cell_drawer_8_img, cell_drawer_9_img, cell_drawer_10_img,
       cell_drawer_11_img, cell_drawer_12_img, cell_drawer_13_img, cell_drawer_14_img, cell_drawer_15_img,
       cell_drawer_16_img, cell_drawer_17_img, cell_drawer_18_img, cell_drawer_19_img, cell_drawer_20_img,
       cell_drawer_21_img, cell_drawer_22_img, cell_drawer_23_img, cell_drawer_24_img, cell_drawer_25_img,
       cell_drawer_26_img, cell_drawer_27_img, cell_drawer_28_img, cell_drawer_29_img, cell_drawer_30_img,
       cell_drawer_31_img, cell_drawer_32_img, cell_drawer_33_img, cell_drawer_34_img, cell_drawer_35_img,
       cell_drawer_36_img, cell_drawer_37_img, cell_drawer_38_img, cell_drawer_39_img, cell_drawer_40_img,
       cell_drawer_41_img, cell_drawer_42_img, cell_drawer_43_img, cell_drawer_44_img, cell_drawer_45_img,
       cell_drawer_46_img, cell_drawer_47_img, cell_drawer_48_img, cell_drawer_49_img, cell_drawer_50_img,
       cell_drawer_51_img, cell_drawer_52_img, cell_drawer_53_img, cell_drawer_54_img, cell_drawer_55_img,
       cell_drawer_56_img, cell_drawer_57_img, cell_drawer_58_img, cell_drawer_59_img, cell_drawer_60_img,
       cell_drawer_61_img, cell_drawer_62_img, cell_drawer_63_img, cell_drawer_64_img;
  wire [7:0] _0x00, _0x01, _0x02, _0x03, _0x04, _0x05, _0x06, _0x07, _0x08, _0x09, _0x10, _0x11, _0x12,
       _0x13, _0x14, _0x15, _0x16, _0x17, _0x18, _0x19, _0x20, _0x21, _0x22, _0x23, _0x24, _0x25, _0x26,
       _0x27, _0x28, _0x29, _0x30, _0x31;

  Button button (.out(w_key));
  Button v (.out(s_key));
  Button button_2 (.out(a_key));
  Button R (.out(r_key));
  Button button_3 (.out(flag_key));
  Button button_4 (.out(open_key));
  Button button_5 (.out(d_key));
  cell_drawer cell_drawer_1 (
    .selected(cell_drawer_1_selected), .img(cell_drawer_1_img), .cell_data(_0x00),
    .explose(cell_drawer_1_explose));
  Hex_Digit_Display hex_digit_display_1 (.value(cell_drawer_1_img), .dp(cell_drawer_1_selected));
  Hex_Digit_Display hex_digit_display_2 (.value(cell_drawer_2_img), .dp(cell_drawer_2_selected));
  cell_drawer cell_drawer_2 (
    .selected(cell_drawer_2_selected), .img(cell_drawer_2_img), .cell_data(_0x08),
    .explose(cell_drawer_2_explose));
  Hex_Digit_Display hex_digit_display_3 (.value(cell_drawer_3_img), .dp(cell_drawer_3_selected));
  cell_drawer cell_drawer_3 (
    .selected(cell_drawer_3_selected), .img(cell_drawer_3_img), .cell_data(_0x16),
    .explose(cell_drawer_3_explose));
  Hex_Digit_Display hex_digit_display_4 (.value(cell_drawer_4_img), .dp(cell_drawer_4_selected));
  cell_drawer cell_drawer_4 (
    .selected(cell_drawer_4_selected), .img(cell_drawer_4_img), .cell_data(_0x24),
    .explose(cell_drawer_4_explose));
  Hex_Digit_Display hex_digit_display_5 (.value(cell_drawer_5_img), .dp(cell_drawer_5_selected));
  cell_drawer cell_drawer_5 (
    .selected(cell_drawer_5_selected), .img(cell_drawer_5_img), .cell_data(_0x00),
    .explose(cell_drawer_5_explose));
  Hex_Digit_Display hex_digit_display_6 (.value(cell_drawer_6_img), .dp(cell_drawer_6_selected));
  cell_drawer cell_drawer_6 (
    .selected(cell_drawer_6_selected), .img(cell_drawer_6_img), .cell_data(_0x08),
    .explose(cell_drawer_6_explose));
  cell_drawer cell_drawer_7 (
    .selected(cell_drawer_7_selected), .img(cell_drawer_7_img), .cell_data(_0x16),
    .explose(cell_drawer_7_explose));
  Hex_Digit_Display hex_digit_display_7 (.value(cell_drawer_7_img), .dp(cell_drawer_7_selected));
  cell_drawer cell_drawer_8 (
    .selected(cell_drawer_8_selected), .img(cell_drawer_8_img), .cell_data(_0x24),
    .explose(cell_drawer_8_explose));
  Hex_Digit_Display hex_digit_display_8 (.value(cell_drawer_8_img), .dp(cell_drawer_8_selected));
  cell_drawer cell_drawer_9 (
    .selected(cell_drawer_9_selected), .img(cell_drawer_9_img), .cell_data(_0x02),
    .explose(cell_drawer_1_explose));
  cell_drawer cell_drawer_10 (
    .selected(cell_drawer_10_selected), .img(cell_drawer_10_img), .cell_data(_0x01),
    .explose(cell_drawer_1_explose));
  Hex_Digit_Display hex_digit_display_9 (.value(cell_drawer_10_img), .dp(cell_drawer_10_selected));
  Hex_Digit_Display hex_digit_display_10 (.value(cell_drawer_9_img), .dp(cell_drawer_9_selected));
  cell_drawer cell_drawer_11 (
    .selected(cell_drawer_11_selected), .img(cell_drawer_11_img), .cell_data(_0x09),
    .explose(cell_drawer_2_explose));
  cell_drawer cell_drawer_12 (
    .selected(cell_drawer_12_selected), .img(cell_drawer_12_img), .cell_data(_0x10),
    .explose(cell_drawer_2_explose));
  Hex_Digit_Display hex_digit_display_11 (.value(cell_drawer_12_img), .dp(cell_drawer_12_selected));
  Hex_Digit_Display hex_digit_display_12 (.value(cell_drawer_11_img), .dp(cell_drawer_11_selected));
  Hex_Digit_Display hex_digit_display_13 (.value(cell_drawer_14_img), .dp(cell_drawer_14_selected));
  cell_drawer cell_drawer_13 (
    .selected(cell_drawer_13_selected), .img(cell_drawer_13_img), .cell_data(_0x18),
    .explose(cell_drawer_3_explose));
  Hex_Digit_Display hex_digit_display_14 (.value(cell_drawer_13_img), .dp(cell_drawer_13_selected));
  cell_drawer cell_drawer_14 (
    .selected(cell_drawer_14_selected), .img(cell_drawer_14_img), .cell_data(_0x17),
    .explose(cell_drawer_3_explose));
  Hex_Digit_Display hex_digit_display_15 (.value(cell_drawer_16_img), .dp(cell_drawer_16_selected));
  cell_drawer cell_drawer_15 (
    .selected(cell_drawer_15_selected), .img(cell_drawer_15_img), .cell_data(_0x25),
    .explose(cell_drawer_4_explose));
  Hex_Digit_Display hex_digit_display_16 (.value(cell_drawer_15_img), .dp(cell_drawer_15_selected));
  cell_drawer cell_drawer_16 (
    .selected(cell_drawer_16_selected), .img(cell_drawer_16_img), .cell_data(_0x26),
    .explose(cell_drawer_4_explose));
  Hex_Digit_Display hex_digit_display_17 (.value(cell_drawer_17_img), .dp(cell_drawer_17_selected));
  Hex_Digit_Display hex_digit_display_18 (.value(cell_drawer_18_img), .dp(cell_drawer_18_selected));
  cell_drawer cell_drawer_17 (
    .selected(cell_drawer_17_selected), .img(cell_drawer_17_img), .cell_data(_0x02),
    .explose(cell_drawer_5_explose));
  cell_drawer cell_drawer_18 (
    .selected(cell_drawer_18_selected), .img(cell_drawer_18_img), .cell_data(_0x01),
    .explose(cell_drawer_5_explose));
  cell_drawer cell_drawer_19 (
    .selected(cell_drawer_19_selected), .img(cell_drawer_19_img), .cell_data(_0x09),
    .explose(cell_drawer_6_explose));
  Hex_Digit_Display hex_digit_display_19 (.value(cell_drawer_20_img), .dp(cell_drawer_20_selected));
  Hex_Digit_Display hex_digit_display_20 (.value(cell_drawer_19_img), .dp(cell_drawer_19_selected));
  cell_drawer cell_drawer_20 (
    .selected(cell_drawer_20_selected), .img(cell_drawer_20_img), .cell_data(_0x10),
    .explose(cell_drawer_6_explose));
  Hex_Digit_Display hex_digit_display_21 (.value(cell_drawer_21_img), .dp(cell_drawer_21_selected));
  Hex_Digit_Display hex_digit_display_22 (.value(cell_drawer_22_img), .dp(cell_drawer_22_selected));
  cell_drawer cell_drawer_21 (
    .selected(cell_drawer_21_selected), .img(cell_drawer_21_img), .cell_data(_0x18),
    .explose(cell_drawer_7_explose));
  cell_drawer cell_drawer_22 (
    .selected(cell_drawer_22_selected), .img(cell_drawer_22_img), .cell_data(_0x17),
    .explose(cell_drawer_7_explose));
  Hex_Digit_Display hex_digit_display_23 (.value(cell_drawer_23_img), .dp(cell_drawer_23_selected));
  cell_drawer cell_drawer_23 (
    .selected(cell_drawer_23_selected), .img(cell_drawer_23_img), .cell_data(_0x25),
    .explose(cell_drawer_8_explose));
  Hex_Digit_Display hex_digit_display_24 (.value(cell_drawer_24_img), .dp(cell_drawer_24_selected));
  cell_drawer cell_drawer_24 (
    .selected(cell_drawer_24_selected), .img(cell_drawer_24_img), .cell_data(_0x26),
    .explose(cell_drawer_8_explose));
  cell_drawer cell_drawer_25 (
    .selected(cell_drawer_25_selected), .img(cell_drawer_25_img), .cell_data(_0x03),
    .explose(cell_drawer_1_explose));
  Hex_Digit_Display hex_digit_display_25 (.value(cell_drawer_25_img), .dp(cell_drawer_25_selected));
  cell_drawer cell_drawer_26 (
    .selected(cell_drawer_26_selected), .img(cell_drawer_26_img), .cell_data(_0x04),
    .explose(cell_drawer_1_explose));
  Hex_Digit_Display hex_digit_display_26 (.value(cell_drawer_27_img), .dp(cell_drawer_27_selected));
  cell_drawer cell_drawer_27 (
    .selected(cell_drawer_27_selected), .img(cell_drawer_27_img), .cell_data(_0x11),
    .explose(cell_drawer_2_explose));
  cell_drawer cell_drawer_28 (
    .selected(cell_drawer_28_selected), .img(cell_drawer_28_img), .cell_data(_0x12),
    .explose(cell_drawer_2_explose));
  Hex_Digit_Display hex_digit_display_27 (.value(cell_drawer_29_img), .dp(cell_drawer_29_selected));
  cell_drawer cell_drawer_29 (
    .selected(cell_drawer_29_selected), .img(cell_drawer_29_img), .cell_data(_0x19),
    .explose(cell_drawer_3_explose));
  cell_drawer cell_drawer_30 (
    .selected(cell_drawer_30_selected), .img(cell_drawer_30_img), .cell_data(_0x20),
    .explose(cell_drawer_3_explose));
  cell_drawer cell_drawer_31 (
    .selected(cell_drawer_31_selected), .img(cell_drawer_31_img), .cell_data(_0x28),
    .explose(cell_drawer_4_explose));
  Hex_Digit_Display hex_digit_display_28 (.value(cell_drawer_32_img), .dp(cell_drawer_32_selected));
  cell_drawer cell_drawer_32 (
    .selected(cell_drawer_32_selected), .img(cell_drawer_32_img), .cell_data(_0x27),
    .explose(cell_drawer_4_explose));
  cell_drawer cell_drawer_33 (
    .selected(cell_drawer_33_selected), .img(cell_drawer_33_img), .cell_data(_0x04),
    .explose(cell_drawer_5_explose));
  Hex_Digit_Display hex_digit_display_29 (.value(cell_drawer_34_img), .dp(cell_drawer_34_selected));
  cell_drawer cell_drawer_34 (
    .selected(cell_drawer_34_selected), .img(cell_drawer_34_img), .cell_data(_0x03),
    .explose(cell_drawer_5_explose));
  cell_drawer cell_drawer_35 (
    .selected(cell_drawer_35_selected), .img(cell_drawer_35_img), .cell_data(_0x12),
    .explose(cell_drawer_6_explose));
  Hex_Digit_Display hex_digit_display_30 (.value(cell_drawer_36_img), .dp(cell_drawer_36_selected));
  cell_drawer cell_drawer_36 (
    .selected(cell_drawer_36_selected), .img(cell_drawer_36_img), .cell_data(_0x11),
    .explose(cell_drawer_6_explose));
  cell_drawer cell_drawer_37 (
    .selected(cell_drawer_37_selected), .img(cell_drawer_37_img), .cell_data(_0x20),
    .explose(cell_drawer_7_explose));
  cell_drawer cell_drawer_38 (
    .selected(cell_drawer_38_selected), .img(cell_drawer_38_img), .cell_data(_0x19),
    .explose(cell_drawer_7_explose));
  Hex_Digit_Display hex_digit_display_31 (.value(cell_drawer_38_img), .dp(cell_drawer_38_selected));
  cell_drawer cell_drawer_39 (
    .selected(cell_drawer_39_selected), .img(cell_drawer_39_img), .cell_data(_0x27),
    .explose(cell_drawer_8_explose));
  cell_drawer cell_drawer_40 (
    .selected(cell_drawer_40_selected), .img(cell_drawer_40_img), .cell_data(_0x28),
    .explose(cell_drawer_8_explose));
  Hex_Digit_Display hex_digit_display_32 (.value(cell_drawer_39_img), .dp(cell_drawer_39_selected));
  cell_drawer cell_drawer_41 (
    .selected(cell_drawer_41_selected), .img(cell_drawer_41_img), .cell_data(_0x05),
    .explose(cell_drawer_1_explose));
  Hex_Digit_Display hex_digit_display_33 (.value(cell_drawer_26_img), .dp(cell_drawer_26_selected));
  Hex_Digit_Display hex_digit_display_34 (.value(cell_drawer_41_img), .dp(cell_drawer_41_selected));
  Hex_Digit_Display hex_digit_display_35 (.value(cell_drawer_42_img), .dp(cell_drawer_42_selected));
  Hex_Digit_Display hex_digit_display_36 (.value(cell_drawer_28_img), .dp(cell_drawer_28_selected));
  cell_drawer cell_drawer_42 (
    .selected(cell_drawer_42_selected), .img(cell_drawer_42_img), .cell_data(_0x13),
    .explose(cell_drawer_2_explose));
  Hex_Digit_Display hex_digit_display_37 (.value(cell_drawer_43_img), .dp(cell_drawer_43_selected));
  Hex_Digit_Display hex_digit_display_38 (.value(cell_drawer_30_img), .dp(cell_drawer_30_selected));
  cell_drawer cell_drawer_43 (
    .selected(cell_drawer_43_selected), .img(cell_drawer_43_img), .cell_data(_0x21),
    .explose(cell_drawer_3_explose));
  Hex_Digit_Display hex_digit_display_39 (.value(cell_drawer_44_img), .dp(cell_drawer_44_selected));
  Hex_Digit_Display hex_digit_display_40 (.value(cell_drawer_31_img), .dp(cell_drawer_31_selected));
  cell_drawer cell_drawer_44 (
    .selected(cell_drawer_44_selected), .img(cell_drawer_44_img), .cell_data(_0x29),
    .explose(cell_drawer_4_explose));
  cell_drawer cell_drawer_45 (
    .selected(cell_drawer_45_selected), .img(cell_drawer_45_img), .cell_data(_0x05),
    .explose(cell_drawer_5_explose));
  Hex_Digit_Display hex_digit_display_41 (.value(cell_drawer_45_img), .dp(cell_drawer_45_selected));
  Hex_Digit_Display hex_digit_display_42 (.value(cell_drawer_33_img), .dp(cell_drawer_33_selected));
  Hex_Digit_Display hex_digit_display_43 (.value(cell_drawer_35_img), .dp(cell_drawer_35_selected));
  Hex_Digit_Display hex_digit_display_44 (.value(cell_drawer_46_img), .dp(cell_drawer_46_selected));
  cell_drawer cell_drawer_46 (
    .selected(cell_drawer_46_selected), .img(cell_drawer_46_img), .cell_data(_0x13),
    .explose(cell_drawer_6_explose));
  cell_drawer cell_drawer_47 (
    .selected(cell_drawer_47_selected), .img(cell_drawer_47_img), .cell_data(_0x21),
    .explose(cell_drawer_7_explose));
  Hex_Digit_Display hex_digit_display_45 (.value(cell_drawer_37_img), .dp(cell_drawer_37_selected));
  Hex_Digit_Display hex_digit_display_46 (.value(cell_drawer_47_img), .dp(cell_drawer_47_selected));
  Hex_Digit_Display hex_digit_display_47 (.value(cell_drawer_48_img), .dp(cell_drawer_48_selected));
  cell_drawer cell_drawer_48 (
    .selected(cell_drawer_48_selected), .img(cell_drawer_48_img), .cell_data(_0x29),
    .explose(cell_drawer_8_explose));
  Hex_Digit_Display hex_digit_display_48 (.value(cell_drawer_40_img), .dp(cell_drawer_40_selected));
  cell_drawer cell_drawer_49 (
    .selected(cell_drawer_49_selected), .img(cell_drawer_49_img), .cell_data(_0x07),
    .explose(cell_drawer_1_explose));
  Hex_Digit_Display hex_digit_display_49 (.value(cell_drawer_49_img), .dp(cell_drawer_49_selected));
  cell_drawer cell_drawer_50 (
    .selected(cell_drawer_50_selected), .img(cell_drawer_50_img), .cell_data(_0x06),
    .explose(cell_drawer_1_explose));
  Hex_Digit_Display hex_digit_display_50 (.value(cell_drawer_50_img), .dp(cell_drawer_50_selected));
  Hex_Digit_Display hex_digit_display_51 (.value(cell_drawer_51_img), .dp(cell_drawer_51_selected));
  cell_drawer cell_drawer_51 (
    .selected(cell_drawer_51_selected), .img(cell_drawer_51_img), .cell_data(_0x15),
    .explose(cell_drawer_2_explose));
  Hex_Digit_Display hex_digit_display_52 (.value(cell_drawer_52_img), .dp(cell_drawer_52_selected));
  cell_drawer cell_drawer_52 (
    .selected(cell_drawer_52_selected), .img(cell_drawer_52_img), .cell_data(_0x14),
    .explose(cell_drawer_2_explose));
  Hex_Digit_Display hex_digit_display_53 (.value(cell_drawer_54_img), .dp(cell_drawer_54_selected));
  cell_drawer cell_drawer_53 (
    .selected(cell_drawer_53_selected), .img(cell_drawer_53_img), .cell_data(_0x23),
    .explose(cell_drawer_3_explose));
  cell_drawer cell_drawer_54 (
    .selected(cell_drawer_54_selected), .img(cell_drawer_54_img), .cell_data(_0x22),
    .explose(cell_drawer_3_explose));
  Hex_Digit_Display hex_digit_display_54 (.value(cell_drawer_53_img), .dp(cell_drawer_53_selected));
  Hex_Digit_Display hex_digit_display_55 (.value(cell_drawer_56_img), .dp(cell_drawer_56_selected));
  cell_drawer cell_drawer_55 (
    .selected(cell_drawer_55_selected), .img(cell_drawer_55_img), .cell_data(_0x31),
    .explose(cell_drawer_4_explose));
  cell_drawer cell_drawer_56 (
    .selected(cell_drawer_56_selected), .img(cell_drawer_56_img), .cell_data(_0x30),
    .explose(cell_drawer_4_explose));
  Hex_Digit_Display hex_digit_display_56 (.value(cell_drawer_55_img), .dp(cell_drawer_55_selected));
  Hex_Digit_Display hex_digit_display_57 (.value(cell_drawer_57_img), .dp(cell_drawer_57_selected));
  cell_drawer cell_drawer_57 (
    .selected(cell_drawer_57_selected), .img(cell_drawer_57_img), .cell_data(_0x06),
    .explose(cell_drawer_5_explose));
  Hex_Digit_Display hex_digit_display_58 (.value(cell_drawer_58_img), .dp(cell_drawer_58_selected));
  cell_drawer cell_drawer_58 (
    .selected(cell_drawer_58_selected), .img(cell_drawer_58_img), .cell_data(_0x07),
    .explose(cell_drawer_5_explose));
  cell_drawer cell_drawer_59 (
    .selected(cell_drawer_59_selected), .img(cell_drawer_59_img), .cell_data(_0x15),
    .explose(cell_drawer_6_explose));
  cell_drawer cell_drawer_60 (
    .selected(cell_drawer_60_selected), .img(cell_drawer_60_img), .cell_data(_0x14),
    .explose(cell_drawer_6_explose));
  Hex_Digit_Display hex_digit_display_59 (.value(cell_drawer_59_img), .dp(cell_drawer_59_selected));
  Hex_Digit_Display hex_digit_display_60 (.value(cell_drawer_60_img), .dp(cell_drawer_60_selected));
  cell_drawer cell_drawer_61 (
    .selected(cell_drawer_61_selected), .img(cell_drawer_61_img), .cell_data(_0x22),
    .explose(cell_drawer_7_explose));
  Hex_Digit_Display hex_digit_display_61 (.value(cell_drawer_62_img), .dp(cell_drawer_62_selected));
  cell_drawer cell_drawer_62 (
    .selected(cell_drawer_62_selected), .img(cell_drawer_62_img), .cell_data(_0x23),
    .explose(cell_drawer_7_explose));
  Hex_Digit_Display hex_digit_display_62 (.value(cell_drawer_61_img), .dp(cell_drawer_61_selected));
  Hex_Digit_Display hex_digit_display_63 (.value(cell_drawer_64_img), .dp(cell_drawer_64_selected));
  cell_drawer cell_drawer_63 (
    .selected(cell_drawer_63_selected), .img(cell_drawer_63_img), .cell_data(_0x30),
    .explose(cell_drawer_8_explose));
  Hex_Digit_Display hex_digit_display_64 (.value(cell_drawer_63_img), .dp(cell_drawer_63_selected));
  cell_drawer cell_drawer_64 (
    .selected(cell_drawer_64_selected), .img(cell_drawer_64_img), .cell_data(_0x31),
    .explose(cell_drawer_8_explose));
endmodule

module processor_hadnler (
);

  wire cdm_8_mark5_1_iack, clock_1_out, mem, undriven;

  Clock clock_1 (.out(clock_1_out));
  CdM_8_mark5 cdm_8_mark5_1 (
    .clock(clock_1_out), .mem_cycle(mem), .IAck(cdm_8_mark5_1_iack), .IRQ(undriven));  // open: addr, mem_read, data_inst, data_out, data_in, r0, r1, r2, r3, PC, SP, PS, vec
endmodule

module cell_drawer (
  input  [7:0] cell_data,
  output [3:0] img,
  output selected,
  output explose
);


  assign explose = 1'b0;
  assign img = 4'b0010;
  assign selected = 1'b0;
endmodule

module map_selector (
  input  map_num
);

  ROM rom_1 ();  // open: addr, data, sel
  ROM rom_2 ();  // open: addr, data, sel
  ROM rom_3 ();  // open: addr, data, sel
  ROM rom_4 ();  // open: addr, data, sel
  ROM rom_5 ();  // open: addr, data, sel
  ROM rom_6 ();  // open: addr, data, sel
endmodule
